# Fritzing sketch tempo_heartrate_turntimer_fritz (saved by Fritzing 0.6.3b)
breadboards: 1

parts:
  J1 = Piezo Speaker
  Arduino_Uno = Arduino
  R2 = Resistor [tolerance=±5% resistance=470 package=THT]
  R1 = Resistor [tolerance=±5% resistance=170 package=THT]
  LED1 = LED - 5mm [color="Red (633nm)" package="5 mm [THT]"]
  LED2 = LED - 5mm [color="Green (565nm)" package="5 mm [THT]"]
  LED3 = LED - 5mm [color="Green (565nm)" package="5 mm [THT]"]
  LED4 = LED - 5mm [color="Green (565nm)" package="5 mm [THT]"]
  R3 = Resistor [tolerance=±5% resistance=820 package=THT]
  R4 = Resistor [tolerance=±5% resistance=820 package=THT]
  R5 = Resistor [tolerance=±5% resistance=820 package=THT]
  Chest_strap_heart_rate_receiver = Chest_strap_heart_rate_receiver

nets:
  N1: J1.pin1, Arduino_Uno.GND, R2.Pin_0, R3.Pin_0, R4.Pin_0, R5.Pin_0, Chest_strap_heart_rate_receiver.connector2
  N2: J1.pin2, R1.Pin_1
  N3: Arduino_Uno.D11, LED2.anode, LED3.anode, LED4.anode
  N4: Arduino_Uno.D6, LED1.cathode
  N5: Arduino_Uno.D4, R1.Pin_0
  N6: Arduino_Uno.D2, Chest_strap_heart_rate_receiver.connector0
  N7: Arduino_Uno.+5V, Chest_strap_heart_rate_receiver.connector1
  N8: R2.Pin_1, LED1.anode
  N9: LED2.cathode, R3.Pin_1
  N10: LED3.cathode, R4.Pin_1
  N11: LED4.cathode, R5.Pin_1
